# Fritzing sketch rotenc-navigator (saved by Fritzing 0.9.4)
breadboards: 1

parts:
  Teensy_LC1 = Teensy-LC
  RE1 = KY-040 Rotary encoder [package=THT]
  RE2 = KY-040 Rotary encoder [package=THT]

nets:
  GND: Teensy_LC1.GND, RE1.GND, RE2.GND
  N1: Teensy_LC1.D2, RE1.DT
  N2: Teensy_LC1.D3, RE1.CLK
  N3: Teensy_LC1.D11, RE2.DT
  N4: Teensy_LC1.D12, Teensy_LC1.5Vout, RE2.CLK
  N5: Teensy_LC1.Program, Teensy_LC1.A12/DAC, Teensy_LC1.D13
  N6: Teensy_LC1.A7/D21, Teensy_LC1.A11
  N7: Teensy_LC1.A8/D22, Teensy_LC1.A10
  N8: Teensy_LC1.A9/D23, Teensy_LC1.AREF
  VCC: Teensy_LC1.3V3, RE1.Vcc, RE2.Vcc
  N9: Teensy_LC1.AGND, Teensy_LC1.VUSB

custom parts:
  Teensy-LC: Teensy-LC (Low Cost) is a powerful 32 bit microcontroller board, with a rich set of hardware peripherals, at a very affordable price! Teensy-LC delivers an impressive collection of capabilities to make modern electronic projects simpler. It features an ARM Cortex-M0+ processor at 48 MHz, 62K Flash, 8K RAM, 12 bit analog input & output, hardware Serial, SPI & I2C, USB, and a total of 27 I/O pins.
  KY-040 Rotary encoder: KY-040 Rotary Encoder with switch on breakout borad from AZ Delivery
